# Fritzing sketch ImprovedSoilMoistureSensorSchematic (saved by Fritzing 0.9.3b)
breadboards: 1

parts:
  Elegoo_Mega2560 = Arduino Mega 2560 (Rev3)
  3_2"_TFT_Touchscreen = 2.4 Touchscreen TFT Breakout w:MicroSD
  Capacitive_Soil_Moisture_Sensor_v1_2 = Soil Moisture Sensor
  SG90 = Basic Servo
  Temperature_&_Humidity_Sensor = DHT11 Humitidy and Temperature Sensor (3 pins)
  Capacitive_Soil_Moisture_Sensor_v1_2_2 = Soil Moisture Sensor

nets:
  N1: Elegoo_Mega2560.A0, 3_2"_TFT_Touchscreen.RD
  N2: Elegoo_Mega2560.A1, 3_2"_TFT_Touchscreen.WR, 3_2"_TFT_Touchscreen.WR_DC
  N3: Elegoo_Mega2560.A2, 3_2"_TFT_Touchscreen.C/D, 3_2"_TFT_Touchscreen.X-
  N4: Elegoo_Mega2560.A3, 3_2"_TFT_Touchscreen.CS, 3_2"_TFT_Touchscreen.Y+
  N5: Elegoo_Mega2560.A6, Capacitive_Soil_Moisture_Sensor_v1_2.SIG
  N6: Elegoo_Mega2560.A7, Capacitive_Soil_Moisture_Sensor_v1_2_2.SIG
  GND: Elegoo_Mega2560.GND, 3_2"_TFT_Touchscreen.GND, Capacitive_Soil_Moisture_Sensor_v1_2.GND, SG90.gnd, Temperature_&_Humidity_Sensor.GND, Capacitive_Soil_Moisture_Sensor_v1_2_2.GND
  N7: Elegoo_Mega2560.RESET, 3_2"_TFT_Touchscreen.RST
  VCC: Elegoo_Mega2560.5V, 3_2"_TFT_Touchscreen.VIN, Capacitive_Soil_Moisture_Sensor_v1_2.VCC, SG90.vcc, Temperature_&_Humidity_Sensor.VDD, Capacitive_Soil_Moisture_Sensor_v1_2_2.VCC
  N8: Elegoo_Mega2560.D2_PWM, Temperature_&_Humidity_Sensor.DATA
  N9: Elegoo_Mega2560.D3_PWM, SG90.pulse
  N10: Elegoo_Mega2560.D22, 3_2"_TFT_Touchscreen.X+, 3_2"_TFT_Touchscreen.D0
  N11: Elegoo_Mega2560.D23, 3_2"_TFT_Touchscreen.Y-, 3_2"_TFT_Touchscreen.D1
  N12: Elegoo_Mega2560.D24, 3_2"_TFT_Touchscreen.D2
  N13: Elegoo_Mega2560.D25, 3_2"_TFT_Touchscreen.D3
  N14: Elegoo_Mega2560.D26, 3_2"_TFT_Touchscreen.D4
  N15: Elegoo_Mega2560.D27, 3_2"_TFT_Touchscreen.D5
  N16: Elegoo_Mega2560.D28, 3_2"_TFT_Touchscreen.D6
  N17: Elegoo_Mega2560.D29, 3_2"_TFT_Touchscreen.D7

notes:
  TFT Touchscreen is 3.2" not 2.4". It also doesn't have the exact same amount of pins, but all the pins are there.
  DHT11 (Temp & Humidity Sensor) is way oversized.
  Plant 2
  Plant 1

custom parts:
  2.4 Touchscreen TFT Breakout w:MicroSD: Add some jazz & pizzazz to your project with a color touchscreen LCD. This TFT display is 2.4" diagonal with a bright (4 white-LED) backlight and it's colorful! 240x320 pixels with individual RGB pixel control, this has way more resolution than a black and white 128x64 display. As a bonus, this display has a resistive touchscreen attached to it already, so you can detect finger presses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
  DHT11 Humitidy and Temperature Sensor (3 pins): DHT11 Humidity and Temperature Sensor (3 pins) from the design created by John De Cristofaro for Adafruit Industries.
